# Fritzing sketch pH Logger (saved by Fritzing 0.9.3b)
circuit board: 15.8049cm x 7.77629cm
breadboards: 1

parts:
  Feather_32u4_Basic = Adafruit Feather 32u4 Basic Proto [part_number="Adafruit #2771"]
  Nokia_5110_LCD_Module1 = Nokia 5110 LCD
  DS18B20 = DS18B20 1-Wire Temperature Sensor [part_number=DS18B20]
  R1 = Resistor [tolerance=±1% resistance=4.7k package=THT]
  FeatherWing_Adalogger = Adafruit Feather 32u4 Adalogger [part_number="Adafruit #2795"]
  S1 = Pushbutton [package="[SMD]"]
  ADS1115 = Adafruit ADS1115 16Bit I2C ADC [part_number="Adafruit #1085"]
  R2 = Resistor [tolerance=±1% resistance=10k package=THT]
  S2 = PH meter [package=THT]

nets:
  GND: Feather_32u4_Basic.GND, S1.Pin_3, S1.Pin_4, ADS1115.GND, S2.pin3
  N1: Nokia_5110_LCD_Module1.RST, FeatherWing_Adalogger.12
  N2: Nokia_5110_LCD_Module1.CE, FeatherWing_Adalogger.11
  N3: Nokia_5110_LCD_Module1.D/C, FeatherWing_Adalogger.A1
  N4: Nokia_5110_LCD_Module1.Din, FeatherWing_Adalogger.A2
  N5: Nokia_5110_LCD_Module1.CLK, FeatherWing_Adalogger.A3
  VCC: Nokia_5110_LCD_Module1.VCC, Nokia_5110_LCD_Module1.BL, R1.Pin_1, FeatherWing_Adalogger.+3V3, ADS1115.AIN0, ADS1115.VDD, R2.Pin_0, S2.pin1
  GND_2: Nokia_5110_LCD_Module1.GND, DS18B20.GND, FeatherWing_Adalogger.GND
  N6: DS18B20.DQ, FeatherWing_Adalogger.6
  N7: DS18B20.VDD, R1.Pin_0
  N8: FeatherWing_Adalogger.5, S1.Pin_1, S1.Pin_2, R2.Pin_1
  N9: FeatherWing_Adalogger.3, ADS1115.SCL
  N10: FeatherWing_Adalogger.2, ADS1115.SDA

custom parts:
  Adafruit Feather 32u4 Basic Proto: At the Feather 32u4's heart is at ATmega32u4 clocked at 8 MHz and at 3.3V logic, a chip setup we've had tons of experience with as it's the same as the Flora. This chip has 32K of flash and 2K of RAM, with built in USB so not only does it have a USB-to-Serial program & debug capability built in with no need for an FTDI-like chip, it can also act like a mouse, keyboard, USB MIDI device, etc.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
  Nokia 5110 LCD: Nokia 5110 Graphic 84*48 LCD module <Blue Version>
  Adafruit Feather 32u4 Adalogger: This is the Adafruit Feather 32u4 Adalogger - our take on an 'all-in-one' datalogger (or data-reader) with built in USB and battery charging. Its an Adafruit Feather 32u4 with a microSD holder ready to rock! We have other boards in the Feather family, check'em out here At the Feather 32u4's heart is at ATmega32u4 clocked at 8 MHz and at 3.3V logic, a chip setup we've had tons of experience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
  Adafruit ADS1115 16Bit I2C ADC: For microcontrollers without an analog-to-digital converter or when you want a higher-precision ADC, the ADS1115 provides 16-bit precision at 860 samples/second over I2C. The chip can be configured as 4 single-ended input channels, or two differential channels. As a nice bonus, it even includes a programmable gain amplifier, up to x16, to help boost up smaller single/differential signals to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
